// Logisim project basic-computer.circ as structural Verilog: 2 circuits, main circuit main
module ALU (
  input  in_1,
  input  [15:0] Input_1__AC,
  input  [15:0] Input_2__DR,
  input  in_4,
  input  [2:0] Selection_of_ALU,
  output out_6,
  output out_7,
  output [15:0] ALU_Output
);

  wire [15:0] adder_1_out, and_1_out, Complement_AC__DR_is_also_correct_out, or_1_out, subtractor_1_out,
       xor_1_out;

  Adder #(.width(16)) adder_1 (.a(Input_1__AC), .b(Input_2__DR), .out(adder_1_out), .cin(in_1), .cout(out_6));
  Subtractor #(.width(16)) subtractor_1 (
    .a(Input_1__AC), .b(Input_2__DR), .out(subtractor_1_out), .bin(in_4), .bout(out_7));
  assign and_1_out = Input_1__AC & Input_2__DR;  // AND_Gate and_1, 16 bits wide
  assign or_1_out = Input_1__AC | Input_2__DR;  // OR_Gate or_1, 16 bits wide
  assign xor_1_out = Input_1__AC ^ Input_2__DR;  // XOR_Gate xor_1, 16 bits wide
  assign Complement_AC__DR_is_also_correct_out = ~Input_1__AC;  // NOT_Gate Complement_AC__DR_is_also_correct, 16 bits wide
  Multiplexer #(.select(3), .width(16)) multiplexer_1 (
    .in0(adder_1_out), .in1(subtractor_1_out), .in2(Input_2__DR), .in3(and_1_out), .in4(or_1_out),
    .in5(xor_1_out), .in6(Complement_AC__DR_is_also_correct_out), .out(ALU_Output), .sel(Selection_of_ALU));  // open: in7, en
endmodule

module main (
  input  in_1,
  input  in_2,
  input  in_3,
  output out_4,
  output out_5
);

  wire AC_LD_out, and_1_out, AR_LD_out, bitselector_1_out, bitselector_2_out, Bline_Mem_out, clock_1_out,
       D0T4_out, D0T5_out, D1T4_out, D1T5_2_out, D1T5_out, D2T4_out, D2T5_2_out, D2T5_out, D3T4_2_out,
       D3T4_out, D4T4_2_out, D4T4_out, D5T4_out, D5T5_out, D7T3_out, d_ff_1_q, decoder_1_out0,
       decoder_1_out1, decoder_1_out2, decoder_1_out3, decoder_1_out4, decoder_1_out5, decoder_1_out7,
       decoder_2_out0, decoder_2_out1, decoder_2_out2, decoder_2_out3, decoder_2_out4, decoder_2_out5,
       DR_LD_out, IncPC_out, M_AR__LD_out, nor_1_out, not_1_out, s_r_ff_1_q, SC_CLR_out, SZA_out;
  wire [2:0] priority_encoder_1_out, priority_encoder_2_out;
  wire [3:0] counter_1_q;
  wire [11:0] AR_q, bit_extender_1_out, bit_extender_2_out, PC_q;
  wire [15:0] AC_q, alu_1_alu_output, bit_extender_3_out, bit_extender_4_out, DR_q, IR_q, multiplexer_1_out,
       ram_1_data, TR_q;

  Clock clock_1 (.out(clock_1_out));
  BitSelector #(.width(12)) bitselector_1 (.in(IR_q[11:0]), .out(bitselector_1_out), .sel(4'b0000));
  and and_1 (and_1_out, decoder_1_out7, bitselector_1_out);
  not not_1 (not_1_out, and_1_out);
  S_R_Flip_Flop s_r_ff_1 (
    .S(not_1_out), .clk(clock_1_out), .R(and_1_out), .Q(s_r_ff_1_q));  // open: Qn, preset, reset, en
  Bit_Extender #(.in_width(16), .out_width(12)) bit_extender_1 (.in(multiplexer_1_out), .out(bit_extender_1_out));
  and SZA (SZA_out, nor_1_out, D7T3_out, bitselector_2_out);
  Bit_Extender #(.in_width(16), .out_width(12)) bit_extender_2 (.in(multiplexer_1_out), .out(bit_extender_2_out));
  Counter #(.width(4), .max('hf)) counter_1 (
    .count(s_r_ff_1_q), .Q(counter_1_q), .clk(clock_1_out), .clr(d_ff_1_q));  // open: load, D, carry
  D_Flip_Flop d_ff_1 (.clk(clock_1_out), .D(SC_CLR_out), .Q(d_ff_1_q));  // open: Qn, preset, en, reset
  Register #(.width(16)) AC (.D(alu_1_alu_output), .en(AC_LD_out), .Q(AC_q), .clk(clock_1_out));  // open: clr
  Register #(.width(16)) DR (.D(multiplexer_1_out), .en(DR_LD_out), .Q(DR_q), .clk(clock_1_out));  // open: clr
  Register #(.width(12)) AR (.D(bit_extender_1_out), .en(AR_LD_out), .Q(AR_q), .clk(clock_1_out));  // open: clr
  Register #(.width(16)) TR (.D(multiplexer_1_out), .en(in_3), .Q(TR_q), .clk(clock_1_out));  // open: clr
  Register #(.width(16)) IR (.D(multiplexer_1_out), .en(decoder_2_out1), .Q(IR_q), .clk(clock_1_out));  // open: clr
  RAM #(.addrWidth(12), .dataWidth(16), .bus("separate")) ram_1 (
    .addr(AR_q), .din(multiplexer_1_out), .data(ram_1_data), .str(M_AR__LD_out), .clk(clock_1_out),
    .ld(Bline_Mem_out));  // open: sel, clr
  ALU alu_1 (
    .in_1(in_1), .Input_1__AC(AC_q), .Input_2__DR(DR_q), .in_4(in_2),
    .Selection_of_ALU(priority_encoder_2_out), .out_6(out_4), .out_7(out_5), .ALU_Output(alu_1_alu_output));
  Counter #(.width(12), .max('hfff)) PC (
    .load(D4T4_out), .D(bit_extender_2_out), .count(IncPC_out), .Q(PC_q), .clk(clock_1_out));  // open: carry, clr
  Decoder #(.select(3), .enable("false")) decoder_1 (
    .out0(decoder_1_out0), .out1(decoder_1_out1), .out2(decoder_1_out2), .out3(decoder_1_out3),
    .out4(decoder_1_out4), .out5(decoder_1_out5), .out7(decoder_1_out7), .sel(IR_q[14:12]));  // open: out6
  Decoder #(.select(4)) decoder_2 (
    .out0(decoder_2_out0), .out1(decoder_2_out1), .out2(decoder_2_out2), .out3(decoder_2_out3),
    .out4(decoder_2_out4), .out5(decoder_2_out5), .sel(counter_1_q));  // open: out6, out7, out8, out9, out10, out11, out12, out13, out14, out15, en
  and D5T5 (D5T5_out, decoder_2_out5, decoder_1_out5);
  assign bit_extender_3_out = {{4{1'b0}}, PC_q};  // Bit_Extender bit_extender_3
  BitSelector #(.width(12)) bitselector_2 (.in(IR_q[11:0]), .out(bitselector_2_out), .sel(4'b0010));
  assign bit_extender_4_out = {{4{1'b0}}, AR_q};  // Bit_Extender bit_extender_4
  and D3T4 (D3T4_out, decoder_1_out3, decoder_2_out4);
  and D2T5 (D2T5_out, decoder_2_out5, decoder_1_out2);
  or IncPC (IncPC_out, SZA_out, decoder_2_out2);
  and D0T4 (D0T4_out, decoder_2_out4, decoder_1_out0);
  and D4T4 (D4T4_out, decoder_1_out4, decoder_2_out4);
  and D1T5 (D1T5_out, decoder_2_out5, decoder_1_out1);
  or SC_CLR (SC_CLR_out, SZA_out, D5T5_out, D2T5_out, D0T5_out, D1T5_out, D4T4_2_out, D3T4_2_out, D7T3_out);
  Multiplexer #(.select(3), .width(16)) multiplexer_1 (
    .in0(AC_q), .in1(DR_q), .in2(TR_q), .in3(bit_extender_4_out), .in4(ram_1_data), .in5(bit_extender_3_out),
    .in6(IR_q), .out(multiplexer_1_out), .sel(priority_encoder_1_out));  // open: in7, en
  and D5T4 (D5T4_out, decoder_1_out5, decoder_2_out4);
  and D7T3 (D7T3_out, decoder_1_out7, decoder_2_out3);
  and D4T4_2 (D4T4_2_out, decoder_2_out4, decoder_1_out4);
  and D3T4_2 (D3T4_2_out, decoder_2_out4, decoder_1_out3);
  and D1T4 (D1T4_out, decoder_1_out1, decoder_2_out4);
  and D2T4 (D2T4_out, decoder_1_out2, decoder_2_out4);
  and D1T5_2 (D1T5_2_out, decoder_1_out1, decoder_2_out5);
  and D2T5_2 (D2T5_2_out, decoder_1_out2, decoder_2_out5);
  or AR_LD (AR_LD_out, decoder_2_out2, decoder_2_out0);
  nor nor_1 (nor_1_out, AC_q[0], AC_q[1], AC_q[2], AC_q[3], AC_q[4], AC_q[5], AC_q[6], AC_q[7], AC_q[8], AC_q[9], AC_q[10], AC_q[11], AC_q[12], AC_q[13], AC_q[14], AC_q[15]);
  Priority_Encoder priority_encoder_1 (
    .in0(D3T4_out), .in3(D4T4_out), .in4(Bline_Mem_out), .in5(decoder_2_out0), .in6(decoder_2_out2),
    .out(priority_encoder_1_out));  // open: in1, in2, in7, en_in
  or DR_LD (DR_LD_out, D0T4_out, D1T4_out, D2T4_out, D5T4_out);
  or AC_LD (AC_LD_out, D0T5_out, D1T5_2_out, D5T5_out, D2T5_2_out);
  buf M_AR__LD (M_AR__LD_out, D3T4_out);  // OR_Gate
  Priority_Encoder priority_encoder_2 (
    .in0(D1T5_2_out), .in1(D5T5_out), .in2(D2T5_2_out), .in3(D0T5_out), .out(priority_encoder_2_out));  // open: in4, in5, in6, in7, en_in, gs, en_out
  // Probe on priority_encoder_2_out
  or Bline_Mem (Bline_Mem_out, D1T4_out, D0T4_out, D5T4_out, decoder_2_out1, D2T4_out);
  and D0T5 (D0T5_out, decoder_2_out5, decoder_1_out0);

  // Notes on the sheet:
  //   SC
  //   T
  //   D
endmodule
